# Fritzing sketch RasPi_Morse_Fritzing_file (saved by Fritzing 0.8.3b)
breadboards: 1

parts:
  LED1 = LED - 5mm [color="Blue (525nm)" package="5 mm [THT]"]
  part = Resistor [tolerance=±5% resistance=220 package=THT]
  Piezo_Buzzer = Piezo Speaker
  Raspberry_Pi_rev2 = Raspberry Pi rev2

nets:
  N1: LED1.cathode, Piezo_Buzzer.pin1, Raspberry_Pi_rev2.GND
  N2: LED1.anode, part.Pin_0
  N3: part.Pin_1, Piezo_Buzzer.pin2, Raspberry_Pi_rev2.GPIO_17
